# Fritzing sketch so_do (saved by Fritzing 0.9.5d)
breadboards: 1

parts:
  Part1 = FTDI Basic Programmer
  ESP32-CAM-CH1 = ESP32-CAM-CH340
  L1 = Solenoid
  VCC1 = Battery block 9V
  LED1 = LED - 5mm [color="Red (633nm)" package="5 mm [THT]"]
  LED2 = LED - 5mm [color="Red (633nm)" package="5 mm [THT]"]
  IC1 = Voltage Regulator [package=78xxl]
  Part2 = Jtron 1 Channel Optoisolated Relay Module [package=relay]

nets:
  N1: Part1.DTR, ESP32-CAM-CH1.GND#16
  N2: Part1.RXI, ESP32-CAM-CH1.GPIO1_/_TX
  N3: Part1.TXO, ESP32-CAM-CH1.GPIO3_/_RX
  N4: Part1.POWER, ESP32-CAM-CH1.3.3V
  N5: ESP32-CAM-CH1.GPIO2, Part2.VCC
  N6: ESP32-CAM-CH1.GPIO13, LED1.anode
  N7: ESP32-CAM-CH1.GPIO12, LED2.anode
  GND: ESP32-CAM-CH1.GND#7, L1.pin1, VCC1.-, LED1.cathode, LED2.cathode, IC1.GND, Part2.GND
  N8: ESP32-CAM-CH1.5V, IC1.OUT, Part2.IN
  N9: ESP32-CAM-CH1.GPIO0, ESP32-CAM-CH1.GND#12
  N10: L1.pin2, Part2.MAIN
  N11: VCC1.+, IC1.IN, Part2.NO

notes:
  led green
  led red
  12V DC Power
  12V Solenoid Lock
  5V DC

custom parts:
  ESP32-CAM-CH340: Versión de ESP-32-CAM que incluye puerto USB.
